// Digital circuit risc-v2_SIMD.dig as structural Verilog
module risc_v2_SIMD (
  input  clk,
  input  in_2
);

  wire and_1_out, and_2_out, and_3_out, not_1_out, or_1_out, u_ALU_Control_beq_bne, u_ALU_f_zero,
       u_Control_Unit_alusrc, u_Control_Unit_branch, u_Control_Unit_jumpreg, u_Control_Unit_memread,
       u_Control_Unit_memtoreg, u_Control_Unit_memwrite, u_Control_Unit_mode, u_Control_Unit_regwrite,
       u_Control_Unit_soma_pc, u_EXMEM_branch_out, u_EXMEM_jalr_ou_jal_out, u_EXMEM_memread_out,
       u_EXMEM_memtoreg_out, u_EXMEM_memwrite_out, u_EXMEM_regwrite_out, u_EXMEM_zero_out, u_Hazard_stall,
       u_IDEX_alusrc_out, u_IDEX_branch_out, u_IDEX_jumpreg_out, u_IDEX_memread_out, u_IDEX_memtoreg_out,
       u_IDEX_memwrite_out, u_IDEX_mode_out, u_IDEX_regwrite_out, u_IDEX_soma_pc_out, u_MEMWB_memtoreg_out,
       u_MEMWB_regwrite_out;
  wire [1:0] u_Control_Unit_aluop, u_Control_Unit_vecsize, u_Forward_forwarda, u_Forward_forwardb,
       u_IDEX_aluop_out, u_IDEX_vecsize_out;
  wire [2:0] u_Control_Unit_s_funct3, u_IDEX_funct3_out;
  wire [3:0] u_ALU_Control_alu_controle;
  wire [4:0] u_EXMEM_rd_out, u_IDEX_rd_out, u_IDEX_rs1_out, u_IDEX_rs2_out, u_IFID_rd, u_IFID_rs1,
       u_IFID_rs2, u_MEMWB_rd_out;
  wire [6:0] u_Control_Unit_s_funct7, u_Control_Unit_s_opcode, u_IDEX_funct7_out, u_IDEX_opcode_out;
  wire [23:0] u_PC4_pc_out;
  wire [31:0] multiplexer_1_out, multiplexer_2_out, multiplexer_3_out, multiplexer_4_out, multiplexer_5_out,
       multiplexer_6_out, multiplexer_7_out, multiplexer_8_out, ramdualport_1_d, ROM_d, u_ALU_resultado,
       u_EXMEM_aluresult_out, u_EXMEM_new_pc_out, u_EXMEM_read2_out, u_IDEX_immediate_out, u_IDEX_pc_out,
       u_IDEX_read1_out, u_IDEX_read2_out, u_IFID_instruction_out, u_IFID_pc4_out, u_IFID_pc_out,
       u_ImmGen_immediate, u_MEMWB_aluresult_out, u_MEMWB_mem_data_out, u_RegisterFile_readdata_1,
       u_RegisterFile_readdata_2, u_Somador_z;
  wire [31:24] u_PC4_pc_out_2;

  Multiplexer #(.Bits(32)) multiplexer_1 (
    .sel(or_1_out), .in_0({u_PC4_pc_out_2, u_PC4_pc_out}), .in_1(u_EXMEM_new_pc_out), .out(multiplexer_1_out));
  PC4 #(.applicationType("GHDL"), .CodeFile("C:\\Users\\Julia\\Desktop\\Arqcomp\\PC4.vhd")) u_PC4 (
    .CLK(clk), .RESET(in_2), .PC_in(multiplexer_1_out), .WriteEnable(not_1_out),
    .PC_out({u_PC4_pc_out_2, u_PC4_pc_out}));
  ROM #(.AddrBits(24), .Bits(32)) ROM (.A(u_PC4_pc_out), .sel(1'b1), .D(ROM_d));
  IFID #(.applicationType("GHDL")) u_IFID (
    .CLK(clk), .PC_in({u_PC4_pc_out_2, u_PC4_pc_out}), .PC4_in(u_IFID_pc4_out), .WriteEnable(not_1_out),
    .Instruction_In(ROM_d), .PC_out(u_IFID_pc_out), .PC4_out(u_IFID_pc4_out),
    .Instruction_Out(u_IFID_instruction_out), .Rs1(u_IFID_rs1), .Rs2(u_IFID_rs2), .Rd(u_IFID_rd));
  not not_1 (not_1_out, u_Hazard_stall);
  Control_Unit #(.applicationType("GHDL")) u_Control_Unit (
    .instruction(u_IFID_instruction_out), .Stall(u_Hazard_stall), .AluSrc(u_Control_Unit_alusrc),
    .RegWrite(u_Control_Unit_regwrite), .MemToReg(u_Control_Unit_memtoreg), .MemRead(u_Control_Unit_memread),
    .MemWrite(u_Control_Unit_memwrite), .Branch(u_Control_Unit_branch), .Soma_PC(u_Control_Unit_soma_pc),
    .AluOp(u_Control_Unit_aluop), .S_funct7(u_Control_Unit_s_funct7), .S_funct3(u_Control_Unit_s_funct3),
    .S_opcode(u_Control_Unit_s_opcode), .JumpReg(u_Control_Unit_jumpreg), .mode(u_Control_Unit_mode),
    .Vecsize(u_Control_Unit_vecsize));
  RegisterFile #(.applicationType("GHDL")) u_RegisterFile (
    .ReadRegister_1(u_IFID_rs1), .ReadRegister_2(u_IFID_rs2), .WriteRegister(u_MEMWB_rd_out),
    .WriteData(multiplexer_8_out), .RegWrite(u_MEMWB_regwrite_out), .CLK(clk),
    .ReadData_1(u_RegisterFile_readdata_1), .ReadData_2(u_RegisterFile_readdata_2));
  ImmGen #(.applicationType("GHDL")) u_ImmGen (.instruction(u_IFID_instruction_out), .immediate(u_ImmGen_immediate));
  Hazard #(.applicationType("GHDL")) u_Hazard (
    .clk(clk), .MemRead_in(u_IDEX_memread_out), .Rd_EX(u_IDEX_rd_out), .Rs1(u_IFID_rs1), .Rs2(u_IFID_rs2),
    .stall(u_Hazard_stall));
  IDEX #(.applicationType("GHDL")) u_IDEX (
    .CLK(clk), .ALUSrc_in(u_Control_Unit_alusrc), .ALUOp_in(u_Control_Unit_aluop),
    .funct3_in(u_Control_Unit_s_funct3), .funct7_in(u_Control_Unit_s_funct7), .PC_in(u_IFID_pc_out),
    .Soma_PC_in(u_Control_Unit_soma_pc), .Branch_in(u_Control_Unit_branch),
    .MemWrite_in(u_Control_Unit_memwrite), .MemRead_in(u_Control_Unit_memread),
    .RegWrite_in(u_Control_Unit_regwrite), .MemToReg_in(u_Control_Unit_memtoreg),
    .read1_in(u_RegisterFile_readdata_1), .read2_in(u_RegisterFile_readdata_2),
    .immediate_in(u_ImmGen_immediate), .Rd_in(u_IFID_rd), .Opcode_in(u_Control_Unit_s_opcode),
    .JumpReg_in(u_Control_Unit_jumpreg), .Rs1_In(u_IFID_rs1), .Rs2_In(u_IFID_rs2),
    .mode_in(u_Control_Unit_mode), .vecsize_in(u_Control_Unit_vecsize), .ALUSrc_out(u_IDEX_alusrc_out),
    .ALUOp_out(u_IDEX_aluop_out), .funct3_out(u_IDEX_funct3_out), .funct7_out(u_IDEX_funct7_out),
    .PC_out(u_IDEX_pc_out), .Soma_PC_out(u_IDEX_soma_pc_out), .Branch_out(u_IDEX_branch_out),
    .MemWrite_out(u_IDEX_memwrite_out), .MemRead_out(u_IDEX_memread_out), .RegWrite_out(u_IDEX_regwrite_out),
    .MemToReg_out(u_IDEX_memtoreg_out), .read1_out(u_IDEX_read1_out), .read2_out(u_IDEX_read2_out),
    .immediate_out(u_IDEX_immediate_out), .Rd_out(u_IDEX_rd_out), .Opcode_out(u_IDEX_opcode_out),
    .JumpReg_out(u_IDEX_jumpreg_out), .Rs1_out(u_IDEX_rs1_out), .Rs2_out(u_IDEX_rs2_out),
    .mode_out(u_IDEX_mode_out), .vecsize_out(u_IDEX_vecsize_out));
  and and_1 (and_1_out, ~u_IDEX_alusrc_out, u_IDEX_soma_pc_out);  // And
  ALU_Control #(.applicationType("GHDL")) u_ALU_Control (
    .Funct7(u_IDEX_funct7_out), .Funct3(u_IDEX_funct3_out), .Opcode(u_IDEX_opcode_out),
    .AluOp(u_IDEX_aluop_out), .ALU_Controle(u_ALU_Control_alu_controle), .Beq_Bne(u_ALU_Control_beq_bne));
  Multiplexer #(.Bits(32)) multiplexer_2 (
    .sel(u_IDEX_alusrc_out), .in_0(u_IDEX_read2_out), .in_1(u_IDEX_immediate_out), .out(multiplexer_2_out));
  Multiplexer #(.Bits(32)) multiplexer_3 (
    .sel(u_IDEX_soma_pc_out), .in_0(u_IDEX_read1_out), .in_1(u_IDEX_pc_out), .out(multiplexer_3_out));
  Multiplexer #(.Bits(32)) multiplexer_4 (
    .sel(and_1_out), .in_0(multiplexer_2_out), .in_1(32'h1), .out(multiplexer_4_out));
  Multiplexer #(.Bits(32)) multiplexer_5 (
    .sel(u_IDEX_jumpreg_out), .in_0(u_IDEX_pc_out), .in_1(u_IDEX_read1_out), .out(multiplexer_5_out));
  Somador #(.applicationType("GHDL")) u_Somador (.A(multiplexer_5_out), .B(u_IDEX_immediate_out), .Z(u_Somador_z));
  Forward #(.applicationType("GHDL")) u_Forward (
    .clk(clk), .regWrite_WB(u_MEMWB_regwrite_out), .regWrite_MEM(u_EXMEM_regwrite_out), .Rs1(u_IDEX_rs1_out),
    .Rs2(u_IDEX_rs2_out), .Rd_WB(u_MEMWB_rd_out), .Rd_Mem(u_EXMEM_rd_out), .forwardA(u_Forward_forwarda),
    .forwardB(u_Forward_forwardb));
  Multiplexer #(.Selector_Bits(2), .Bits(32)) multiplexer_6 (
    .sel(u_Forward_forwarda), .in_0(multiplexer_3_out), .in_1(multiplexer_8_out),
    .in_2(u_EXMEM_aluresult_out), .in_3(32'h1), .out(multiplexer_6_out));
  Multiplexer #(.Selector_Bits(2), .Bits(32)) multiplexer_7 (
    .sel(u_Forward_forwardb), .in_0(multiplexer_4_out), .in_1(multiplexer_8_out),
    .in_2(u_EXMEM_aluresult_out), .in_3(32'h1), .out(multiplexer_7_out));
  ALU #(.applicationType("GHDL")) u_ALU (
    .A(multiplexer_6_out), .B(multiplexer_7_out), .controle(u_ALU_Control_alu_controle),
    .mode(u_IDEX_mode_out), .vecSize(u_IDEX_vecsize_out), .resultado(u_ALU_resultado), .f_zero(u_ALU_f_zero));
  and and_2 (and_2_out, u_ALU_f_zero, u_ALU_Control_beq_bne);
  EXMEM #(.applicationType("GHDL")) u_EXMEM (
    .CLK(clk), .Branch_in(u_IDEX_branch_out), .MemWrite_in(u_IDEX_memwrite_out),
    .MemRead_in(u_IDEX_memread_out), .RegWrite_in(u_IDEX_regwrite_out), .MemToReg_in(u_IDEX_memtoreg_out),
    .New_PC_in(u_Somador_z), .Zero_in(and_2_out), .ALUresult_in(u_ALU_resultado),
    .read2_in(u_IDEX_read2_out), .Rd_in(u_IDEX_rd_out), .Jalr_ou_Jal_in(and_1_out),
    .Branch_out(u_EXMEM_branch_out), .MemWrite_out(u_EXMEM_memwrite_out), .MemRead_out(u_EXMEM_memread_out),
    .RegWrite_out(u_EXMEM_regwrite_out), .MemToReg_out(u_EXMEM_memtoreg_out),
    .New_PC_out(u_EXMEM_new_pc_out), .Zero_out(u_EXMEM_zero_out), .ALUresult_out(u_EXMEM_aluresult_out),
    .read2_out(u_EXMEM_read2_out), .Rd_out(u_EXMEM_rd_out), .Jalr_ou_Jal_out(u_EXMEM_jalr_ou_jal_out));
  and and_3 (and_3_out, u_EXMEM_branch_out, u_EXMEM_zero_out);
  or or_1 (or_1_out, and_3_out, u_EXMEM_jalr_ou_jal_out);
  RAMDualPort #(.AddrBits(24), .Bits(32)) ramdualport_1 (
    .A(u_EXMEM_aluresult_out[23:0]), .Din(u_EXMEM_read2_out), .str(u_EXMEM_memwrite_out), .C(clk),
    .ld(u_EXMEM_memread_out), .D(ramdualport_1_d));
  MEMWB #(.applicationType("GHDL")) u_MEMWB (
    .CLK(clk), .RegWrite_in(u_EXMEM_regwrite_out), .MemToReg_in(u_EXMEM_memtoreg_out),
    .Mem_data_in(ramdualport_1_d), .ALUresult_in(u_EXMEM_aluresult_out), .Rd_in(u_EXMEM_rd_out),
    .RegWrite_out(u_MEMWB_regwrite_out), .MemToReg_out(u_MEMWB_memtoreg_out),
    .Mem_data_out(u_MEMWB_mem_data_out), .ALUresult_out(u_MEMWB_aluresult_out), .Rd_out(u_MEMWB_rd_out));
  Multiplexer #(.Bits(32)) multiplexer_8 (
    .sel(u_MEMWB_memtoreg_out), .in_0(u_MEMWB_aluresult_out), .in_1(u_MEMWB_mem_data_out),
    .out(multiplexer_8_out));
endmodule

/* Code of IFID:
LIBRARY ieee;
USE ieee.std_logic_1164.all;

ENTITY IFID IS
  PORT (
    CLK         : IN  std_logic;                    -- Entrada do CLOCK
    PC_in        : IN  std_logic_vector(31 DOWNTO 0); -- Entrada do valor atual do PC (contador de programa)
    PC4_in	 : IN  std_logic_vector(31 downto 0); -- Entrada do valor do PC mais 4 (próxima instrução)
    WriteEnable   : IN std_logic;                 -- Entrada do sinal de habilitação de escrita no IFID
    Instruction_In      : IN  std_logic_vector(31 DOWNTO 0); -- Entrada da instrução atual buscada na memória de instruções
    PC_out       : OUT std_logic_vector(31 DOWNTO 0); -- Saída do valor atual do PC (contador de programa)
    PC4_out	 : OUT std_logic_vector(31 downto 0); -- Saída do valor do PC mais 4 (próxima instrução)
    Instruction_Out     : OUT std_logic_vector(31 DOWNTO 0);  -- Saída da instrução atual buscada na memória de instruções
    Rs1 : OUT std_logic_vector(4 DOWNTO 0);  -- Saída da instrução atual buscada na memória de instruções
    Rs2 : OUT std_logic_vector(4 DOWNTO 0);  -- Saída da instrução atual buscada na memória de instruções
    Rd : OUT std_logic_vector(4 DOWNTO 0)  -- Saída da instrução atual buscada na memória de instruções
    );
END IFID;


ARCHITECTURE TypeArchitecture OF IFID IS

signal opcode : std_logic_vector(6 downto 0);	-- Opcode da Instrução
signal s_Rs1 : std_logic_vector(4 downto 0);		-- Rs1 da Instrução
signal s_Rs2 : std_logic_vector(4 downto 0);		-- Rs2 da Instrução
signal s_Rd : std_logic_vector(4 downto 0);		-- Rd da Instrução
SIGNAL IDIF : std_logic_vector(117 DOWNTO 0);  	-- Registrador de 96 bits para armazenar os valores do IFID

BEGIN
	-- Definição do Opcode da Instrução
	opcode(0) <= Instruction_In(0);
	opcode(1) <= Instruction_In(1);
	opcode(2) <= Instruction_In(2);
	opcode(3) <= Instruction_In(3);
	opcode(4) <= Instruction_In(4);
	opcode(5) <= Instruction_In(5);
	opcode(6) <= Instruction_In(6);

	process(opcode)
	begin
	-- Rs1
		IF NOT (opcode = "1101111" or opcode = "0110111") THEN  -- Tipos diferentes de U e UJ tem Rs1
		s_Rs1 (0) <= Instruction_In(15);
		s_Rs1 (1) <= Instruction_In(16);
		s_Rs1 (2) <= Instruction_In(17);
		s_Rs1 (3) <= Instruction_In(18);
		s_Rs1 (4) <= Instruction_In(19);
		END IF;

	-- Rs2
		IF (opcode = "0110011" or opcode = "0100011" or opcode = "1100011") THEN  -- Tipos R, S e Sb tem Rs2
		s_Rs2 (0) <= Instruction_In(20);
		s_Rs2 (1) <= Instruction_In(21);
		s_Rs2 (2) <= Instruction_In(22);
		s_Rs2 (3) <= Instruction_In(23);
		s_Rs2 (4) <= Instruction_In(24);
		END IF;

	-- Rd
		IF NOT (opcode = "0100011" or opcode = "1100011") THEN  -- Tipos diferentes de S e Sb tem Rd
		s_Rd (0) <= Instruction_In(7); 
		s_Rd (1) <= Instruction_In(8);
		s_Rd (2) <= Instruction_In(9);
		s_Rd (3) <= Instruction_In(10);
		s_Rd (4) <= Instruction_In(11);
		END IF;
	end process;

	
	PROCESS (CLK, WriteEnable)
	BEGIN
		IF (rising_edge(CLK)) THEN                   	-- Detecção de subida de CLOCK
			if (WriteEnable = '1') then             	-- Vericação se o WriteEnable está habilitado
				IDIF(31 DOWNTO 0) <= Instruction_In;       
				IDIF(63 DOWNTO 32) <= PC_in;          	-- Armazena o valor atual do PC
				IDIF(95 downto 64) <= PC4_in;       	-- Armazena o valor do PC mais 4 (próxima instrução)
				IDIF(102 downto 96) <= opcode;		-- Armazena o opcode
				IDIF(107 downto 103) <= s_Rs1;		-- Armazena o Rs1
				IDIF(112 downto 108) <= s_Rs2;		-- Armazena o Rs2
				IDIF(117 downto 113) <= s_Rd;			-- Armazena o Rd
			end if;
		END IF;
		IF (falling_edge(CLK)) THEN                 		-- Detecção de descida de CLOCK
			PC_out <= IDIF(63 DOWNTO 32);           	-- Definição do PC atual
			Instruction_Out <= IDIF(31 DOWNTO 0);        -- Definição da instrução armazenada
			PC4_out <= IDIF(95 downto 64);        		-- Saída de PC+4
			Rs1 <= IDIF(107 downto 103);				-- Saída do Rs1
			Rs2 <= IDIF(112 downto 108);				-- Saída do Rs2
			Rd <= IDIF(117 downto 113);				-- Saída do Rd
		END IF;
	END PROCESS;
	
END TypeArchitecture;
*/

/* Code of Control_Unit:
library IEEE;
use IEEE.STD_LOGIC_1164.ALL;

entity Control_Unit is
    port(
        instruction                	: IN  std_logic_vector(31 downto 0);  -- Entrada da Instrução
        Stall                			: IN  std_logic;  				   -- Entrada do Hazard
        AluSrc, RegWrite, MemToReg 	: OUT std_logic;                      -- Sinais de Controle (1 Bit)
        MemRead, MemWrite, Branch  	: OUT std_logic;                      -- Sinais de Controle (1 Bit)
        Soma_PC 					: OUT std_logic;			   	   -- Sinais de Controle (1 Bit)	
        AluOp		               	: OUT std_logic_vector(1 downto 0);   -- Saída da Operação da ALU (2 Bits)
        S_funct7 					: OUT std_logic_vector(6 downto 0);   -- Saída do Funct7
        S_funct3 					: OUT std_logic_vector(2 downto 0);   -- Saída do Funct3
        S_opcode 					: OUT std_logic_vector(6 downto 0);   -- Saída do Opcode
        JumpReg					: OUT std_logic;				   -- Indica quando a instrução é jalr	
        mode						: OUT std_logic;				   -- Indica se é uma operação vetorial
        Vecsize					: OUT std_logic_vector(1 downto 0));  -- Indica o tamanho do vetor
        
end Control_Unit;

architecture TypeArchitecture of Control_Unit is

signal opcode : std_logic_vector(6 downto 0);	-- Opcode da Instrução
signal funct7 : std_logic_vector(6 downto 0);	-- Funct7 da Instrução
signal funct3 : std_logic_vector(2 downto 0);	-- Funct3 da Instrução


begin
	-- Definição do Opcode da Instrução
	opcode(0) <= instruction(0);
	opcode(1) <= instruction(1);
	opcode(2) <= instruction(2);
	opcode(3) <= instruction(3);
	opcode(4) <= instruction(4);
	opcode(5) <= instruction(5);
	opcode(6) <= instruction(6);
	Soma_PC <= '0'; 
	JumpReg <= '0';

	process(Stall)
	begin
		IF (Stall = '1') THEN
			AluSrc <= '0';
			RegWrite <= '0';
			MemToReg <= '0';
			MemRead <= '0';
			MemWrite <= '0';
			Branch <= '0';
			Soma_PC <= '0';
			JumpReg <= '0';
		end if; 
	end process;
	-- Definição das Funct7, Funct3 e dos Sinais de Controle de acordo com o opcode.
	process(opcode)
	begin
		IF (opcode = "0110011") THEN		-- R-Type Instruction
			funct7(6) <= instruction(31);
			funct7(5) <= instruction(30);
			funct7(4) <= instruction(29);
			funct7(3) <= instruction(28);
			funct7(2) <= instruction(27);
			funct7(1) <= instruction(26);
			funct7(0) <= instruction(25);
			funct3(2) <= instruction (14);
			funct3(1) <= instruction (13);
			funct3(0) <= instruction (12);
			AluSrc <= '0'; 			
			RegWrite <= '1';
			MemToReg <= '0';
			MemRead <= '0';
			MemWrite <= '0';
			Branch <= '0';
			mode <= '0';
			Vecsize <= "11";
			AluOp <= "10";
		END IF;
		IF (opcode = "0010011") THEN		-- I-Type Instruction (ADDi, ANDi, ORi, XORi, SLTi)
			funct7(6) <= '0';
			funct7(5) <= '0';
			funct7(4) <= '0';
			funct7(3) <= '0';
			funct7(2) <= '0';
			funct7(1) <= '0';
			funct7(0) <= '0';
			funct3(2) <= instruction (14);
			funct3(1) <= instruction (13);
			funct3(0) <= instruction (12);
			AluSrc <= '1'; 			
			RegWrite <= '1';
			MemToReg <= '0';
			MemRead <= '0';
			MemWrite <= '0';
			Branch <= '0';
			mode <= '0';
			Vecsize <= "11";
			AluOp <= "10";
		END IF;
		IF (opcode = "0000011") THEN		-- I-Type Instruction (Load)
			funct7(6) <= '0';
			funct7(5) <= '0';
			funct7(4) <= '0';
			funct7(3) <= '0';
			funct7(2) <= '0';
			funct7(1) <= '0';
			funct7(0) <= '0';
			funct3(2) <= '0';
			funct3(1) <= '0';
			funct3(0) <= '0';
			AluSrc <= '1'; 			
			RegWrite <= '1';
			MemToReg <= '1';
			MemRead <= '1';
			MemWrite <= '0';
			Branch <= '0';
			mode <= '0';
			Vecsize <= "11";
			AluOp <= "00";
		END IF;
		IF (opcode = "1100111") THEN		-- I-Type Instruction (Jump) 
			funct7(6) <= '0';
			funct7(5) <= '0';
			funct7(4) <= '0';
			funct7(3) <= '0';
			funct7(2) <= '0';
			funct7(1) <= '0';
			funct7(0) <= '0';
			funct3(2) <= '0';
			funct3(1) <= '0';
			funct3(0) <= '0';
			AluSrc <= '0'; 			
			RegWrite <= '0';
			MemToReg <= '0';
			MemRead <= '0';
			MemWrite <= '0';
			Branch <= '0';
			Soma_PC <= '1';
			JumpReg <= '1';
			mode <= '0';
			Vecsize <= "11";
			AluOp <= "01";
		END IF;
		IF (opcode = "0100011") THEN		-- S-Type Instruction 
			funct7(6) <= '0';
			funct7(5) <= '0';
			funct7(4) <= '0';
			funct7(3) <= '0';
			funct7(2) <= '0';
			funct7(1) <= '0';
			funct7(0) <= '0';
			funct3(2) <= '0';
			funct3(1) <= '0';
			funct3(0) <= '0';
			AluSrc <= '1'; 			
			RegWrite <= '0';
			MemToReg <= '0';
			MemRead <= '0';
			MemWrite <= '1';
			Branch <= '0';
			mode <= '0';
			Vecsize <= "11";
			AluOp <= "00";
		END IF;
		IF (opcode = "1101111") THEN		-- UJ-Type Instruction (jal)
			funct7(6) <= '0';
			funct7(5) <= '0';
			funct7(4) <= '0';
			funct7(3) <= '0';
			funct7(2) <= '0';
			funct7(1) <= '0';
			funct7(0) <= '0';
			funct3(2) <= '0';
			funct3(1) <= '0';
			funct3(0) <= '0';
			AluSrc <= '0'; 			
			RegWrite <= '1';
			MemToReg <= '0';
			MemRead <= '0';
			MemWrite <= '0';
			Branch <= '0';
			Soma_PC <= '1';
			mode <= '0';
			Vecsize <= "11";
			AluOp <= "10";
		END IF;
		IF (opcode = "0110111") THEN		-- U-Type Instruction (lui - soma com imediato muito grande)
			funct7(6) <= '0';
			funct7(5) <= '0';
			funct7(4) <= '0';
			funct7(3) <= '0';
			funct7(2) <= '0';
			funct7(1) <= '0';
			funct7(0) <= '0';
			funct3(2) <= '0';
			funct3(1) <= '0';
			funct3(0) <= '0';
			AluSrc <= '1'; 			
			RegWrite <= '1';
			MemToReg <= '0';
			MemRead <= '0';
			MemWrite <= '0';
			Branch <= '0';
			mode <= '0';
			Vecsize <= "11";
			AluOp <= "10";
		END IF;
		IF (opcode = "0010111") THEN		-- U-Type Instruction (auipc, soma do pc com o imediato e guarda no registrador)
			funct7(6) <= '0';
			funct7(5) <= '0';
			funct7(4) <= '0';
			funct7(3) <= '0';
			funct7(2) <= '0';
			funct7(1) <= '0';
			funct7(0) <= '0';
			funct3(2) <= '0';
			funct3(1) <= '0';
			funct3(0) <= '0';
			AluSrc <= '1'; 			
			RegWrite <= '1';
			MemToReg <= '0';
			MemRead <= '0';
			MemWrite <= '0';
			Branch <= '0';
			Soma_PC <= '1';
			mode <= '0';
			Vecsize <= "11";
			AluOp <= "10";
		END IF;
		IF (opcode = "1100011") THEN		-- Sb-Type Instruction 
			funct7(6) <= '0';
			funct7(5) <= '0';
			funct7(4) <= '0';
			funct7(3) <= '0';
			funct7(2) <= '0';
			funct7(1) <= '0';
			funct7(0) <= '0';
			funct3(2) <= instruction (14);
			funct3(1) <= instruction (13);
			funct3(0) <= instruction (12);
			AluSrc <= '0'; 			
			RegWrite <= '0';
			MemToReg <= '0';
			MemRead <= '0';
			MemWrite <= '0';
			Branch <= '1';
			mode <= '0';
			Vecsize <= "11";
			AluOp <= "01";
		END IF;
		IF (opcode = "1111100") 	THEN		-- R-Type Vetorial Instruction (4bits)
			funct7(6) <= instruction(31);
			funct7(5) <= instruction(30);
			funct7(4) <= instruction(29);
			funct7(3) <= instruction(28);
			funct7(2) <= instruction(27);
			funct7(1) <= instruction(26);
			funct7(0) <= instruction(25);
			funct3(2) <= instruction (14);
			funct3(1) <= instruction (13);
			funct3(0) <= instruction (12);
			AluSrc <= '0'; 			
			RegWrite <= '1';
			MemToReg <= '0';
			MemRead <= '0';
			MemWrite <= '0';
			Branch <= '0';
			mode <= '1';
			Vecsize <= "00";
			AluOp <= "10";
		END IF;
		IF (opcode = "1111101")  THEN				-- R-Type Vetorial Instruction (8bits)
			funct7(6) <= instruction(31);
			funct7(5) <= instruction(30);
			funct7(4) <= instruction(29);
			funct7(3) <= instruction(28);
			funct7(2) <= instruction(27);
			funct7(1) <= instruction(26);
			funct7(0) <= instruction(25);
			funct3(2) <= instruction (14);
			funct3(1) <= instruction (13);
			funct3(0) <= instruction (12);
			AluSrc <= '0'; 			
			RegWrite <= '1';
			MemToReg <= '0';
			MemRead <= '0';
			MemWrite <= '0';
			Branch <= '0';
			mode <= '1';
			Vecsize <= "01";
			AluOp <= "10";
		END IF;
		IF (opcode = "1111110")	THEN			-- R-Type Vetorial Instruction (16bits)
			funct7(6) <= instruction(31);
			funct7(5) <= instruction(30);
			funct7(4) <= instruction(29);
			funct7(3) <= instruction(28);
			funct7(2) <= instruction(27);
			funct7(1) <= instruction(26);
			funct7(0) <= instruction(25);
			funct3(2) <= instruction (14);
			funct3(1) <= instruction (13);
			funct3(0) <= instruction (12);
			AluSrc <= '0'; 			
			RegWrite <= '1';
			MemToReg <= '0';
			MemRead <= '0';
			MemWrite <= '0';
			Branch <= '0';
			mode <= '1';
			Vecsize <= "10";
			AluOp <= "10";
		END IF;
		IF (opcode = "1111000") THEN		-- I-Type Vetorial Instruction (Soma e deslocamento)(4bits)
			funct7(6) <= '0';
			funct7(5) <= '0';
			funct7(4) <= '0';
			funct7(3) <= '0';
			funct7(2) <= '0';
			funct7(1) <= '0';
			funct7(0) <= '0';
			funct3(2) <= instruction (14);
			funct3(1) <= instruction (13);
			funct3(0) <= instruction (12);
			AluSrc <= '1'; 			
			RegWrite <= '1';
			MemToReg <= '0';
			MemRead <= '0';
			MemWrite <= '0';
			Branch <= '0';
			mode <= '1';
			Vecsize <= "00";
			AluOp <= "10";
		END IF;
		IF (opcode = "1111001") THEN		-- I-Type Vetorial Instruction (Soma e deslocamento)(8bits)
			funct7(6) <= '0';
			funct7(5) <= '0';
			funct7(4) <= '0';
			funct7(3) <= '0';
			funct7(2) <= '0';
			funct7(1) <= '0';
			funct7(0) <= '0';
			funct3(2) <= instruction (14);
			funct3(1) <= instruction (13);
			funct3(0) <= instruction (12);
			AluSrc <= '1'; 			
			RegWrite <= '1';
			MemToReg <= '0';
			MemRead <= '0';
			MemWrite <= '0';
			Branch <= '0';
			mode <= '1';
			Vecsize <= "01";
			AluOp <= "10";
		END IF;
		IF (opcode = "1111010") THEN		-- I-Type Vetorial Instruction (Soma e deslocamento)(16bits)
			funct7(6) <= '0';
			funct7(5) <= '0';
			funct7(4) <= '0';
			funct7(3) <= '0';
			funct7(2) <= '0';
			funct7(1) <= '0';
			funct7(0) <= '0';
			funct3(2) <= instruction (14);
			funct3(1) <= instruction (13);
			funct3(0) <= instruction (12);
			AluSrc <= '1'; 			
			RegWrite <= '1';
			MemToReg <= '0';
			MemRead <= '0';
			MemWrite <= '0';
			Branch <= '0';
			mode <= '1';
			Vecsize <= "10";
			AluOp <= "10";
		END IF;
		IF (opcode = "1110000") THEN		-- U-Type Vetorial Instruction (4bits)(auipc)
			funct7(6) <= '0';
			funct7(5) <= '0';
			funct7(4) <= '0';
			funct7(3) <= '0';
			funct7(2) <= '0';
			funct7(1) <= '0';
			funct7(0) <= '0';
			funct3(2) <= '0';
			funct3(1) <= '0';
			funct3(0) <= '0';
			AluSrc <= '1'; 			
			RegWrite <= '1';
			MemToReg <= '0';
			MemRead <= '0';
			MemWrite <= '0';
			Branch <= '0';
			Soma_PC <= '1';
			mode <= '1';
			Vecsize <= "00";
			AluOp <= "10";
		END IF;
		IF (opcode = "1110001") THEN		-- U-Type Vetorial Instruction (4bits)(auipc)
			funct7(6) <= '0';
			funct7(5) <= '0';
			funct7(4) <= '0';
			funct7(3) <= '0';
			funct7(2) <= '0';
			funct7(1) <= '0';
			funct7(0) <= '0';
			funct3(2) <= '0';
			funct3(1) <= '0';
			funct3(0) <= '0';
			AluSrc <= '1'; 			
			RegWrite <= '1';
			MemToReg <= '0';
			MemRead <= '0';
			MemWrite <= '0';
			Branch <= '0';
			Soma_PC <= '1';
			mode <= '1';
			Vecsize <= "01";
			AluOp <= "10";
		END IF;
		IF (opcode = "1110010") THEN		-- U-Type Vetorial Instruction (4bits)(auipc)
			funct7(6) <= '0';
			funct7(5) <= '0';
			funct7(4) <= '0';
			funct7(3) <= '0';
			funct7(2) <= '0';
			funct7(1) <= '0';
			funct7(0) <= '0';
			funct3(2) <= '0';
			funct3(1) <= '0';
			funct3(0) <= '0';
			AluSrc <= '1'; 			
			RegWrite <= '1';
			MemToReg <= '0';
			MemRead <= '0';
			MemWrite <= '0';
			Branch <= '0';
			Soma_PC <= '1';
			mode <= '1';
			Vecsize <= "10";
			AluOp <= "10";
		END IF;
	end process;
	S_funct7 <= funct7;
	S_funct3 <= funct3;
	S_opcode <= opcode;
end TypeArchitecture;
*/

/* Code of RegisterFile:
library ieee;
use ieee.std_logic_1164.all;
use ieee.numeric_std.all;

entity RegisterFile is
  port(
    ReadRegister_1           : in std_logic_vector(4 downto 0);    	-- Endereço do primeiro registrador a ser lido
    ReadRegister_2           : in std_logic_vector(4 downto 0);    	-- Endereço do segundo registrador a ser lido
    WriteRegister      	    : in std_logic_vector(4 downto 0);    	-- Endereço do registrador a ser escrito
    WriteData                : in  std_logic_vector(31 downto 0);     -- Dado a ser escrito
    RegWrite  			    : in  std_logic;     				    -- Sinal de controle
    ReadData_1         	    : out  std_logic_vector(31 downto 0);    -- Dado do primeiro registrador lido
    ReadData_2       	    : out  std_logic_vector(31 downto 0);    -- Dado do segundo registrador lido
    CLK                 	    : in  std_logic                        	-- Sinal do CLOCK
    );
end RegisterFile;

architecture TypeArchitecture of RegisterFile is
  type RegisterArray is array(0 to 31) of std_logic_vector(31 downto 0);
  signal Registers : RegisterArray := 
   ("00000000000000000000000000000000","00000000000000000000000000000000","00000000000000000000000000000000","00000000000000000000000000000000",
    "00000000000000000000000000000000","00000000000000000000000000000000","00000000000000000000000000000000","00000000000000000000000000000000",
    "00000000000000000000000000000000","00000000000000000000000000000000","00000000000000000000000000000000","00000000000000000000000000000000",
    "00000000000000000000000000000000","00000000000000000000000000000000","00000000000000000000000000000000","00000000000000000000000000000000",
    "00000000000000000000000000000000","00000000000000000000000000000000","00000000000000000000000000000000","00000000000000000000000000000000",
    "00000000000000000000000000000000","00000000000000000000000000000000","00000000000000000000000000000000","00000000000000000000000000000000",
    "00000000000000000000000000000000","00000000000000000000000000000000","00000000000000000000000000000000","00000000000000000000000000000000",
    "00000000000000000000000000000000","00000000000000000000000000000000","00000000000000000000000000000000","00000000000000000000000000000000");

begin
  regFile : process (CLK) is
  begin
    if falling_edge(CLK) then
      if (Registers(to_integer(unsigned(ReadRegister_1))) = "UUUUUUUUUUUUUUUUUUUUUUUUUUUUUUUU") THEN -- Caso o valor do registrador esteja indefinido, a saída será "000..."
      	ReadData_1 <= (others => '0');  
      ELSE 
      	ReadData_1 <= Registers(to_integer(unsigned(ReadRegister_1)));  -- Leitura do valor contido no registrador 1
      END IF;
      IF (Registers(to_integer(unsigned(ReadRegister_2))) = "UUUUUUUUUUUUUUUUUUUUUUUUUUUUUUUU") THEN -- Caso o valor do registrador esteja indefinido, a saída será "000..."
      	ReadData_2 <= (others => '0');  
      ELSE
      	ReadData_2 <= Registers(to_integer(unsigned(ReadRegister_2)));  -- Leitura do valor contido no registrador 2 
      END IF;
    end if; 
    if rising_edge(CLK) then
      if RegWrite = '1' then
        Registers(to_integer(unsigned(WriteRegister))) <= WriteData;      -- Escrita do valor no registrador selecionado
      end if;
    end if;
  end process;
  
end TypeArchitecture;
*/

/* Code of ImmGen:
library IEEE;
use IEEE.STD_LOGIC_1164.ALL;
USE IEEE.NUMERIC_STD.ALL;

entity ImmGen is
    Port( 
        instruction: in std_logic_vector(31 downto 0);  	-- Entrada da Instrução 
        immediate: out std_logic_vector(31 downto 0)  		-- Saída do Valor Imediato
        );
end ImmGen;

architecture Behavioral of ImmGen is
    signal opcode       : std_logic_vector(6 downto 0);  		-- Sinal para armazenr o opcode da instrução
    signal S_imm  : std_logic_vector(31 downto 0) := "00000000000000000000000000000000";  -- Sinal auxiliar para definição do imediato

begin

    opcode <= instruction(6 downto 0);  -- Definição do opcode

    process(opcode)
    begin
        if (opcode = "0010011" or opcode = "0000011" or opcode = "1100111") then  	-- Tipo I 
            S_imm(11 downto 0)  <= instruction(31 downto 20);  					-- Seleciona o imediato 
            S_imm(31 downto 12) <= (others => instruction(31));  				-- Extensão do Bit de Sinal
        elsif (opcode = "1101111") then  									-- Tipo UJ 
            S_imm(20) <= instruction(31);  									-- Seleciona o imediato
            S_imm(10 downto 1) <= instruction(30 downto 21);					-- Seleciona o imediato
            S_imm(11) <= instruction(20);									-- Seleciona o imediato	
            S_imm(19 downto 12) <= instruction(19 downto 12);					-- Seleciona o imediato
            S_imm(31 downto 21) <= (others => instruction(31));					-- Extensão do Bit de Sinal
        elsif (opcode = "0110111" or opcode = "0010111") then										-- Tipo U 
        	  S_imm(31 downto 12) <= instruction(31 downto 12);  					-- Seleciona o imediato	
        elsif (opcode = "0100011") then  									-- Tipo S 
            S_imm(11 downto 5)  <= instruction(31 downto 25);  					-- Seleciona o imediato
            S_imm(4 downto 0)   <= instruction(11 downto 7);   					-- Seleciona o imediato
            S_imm(31 downto 12) <= (others => instruction(31));  				-- Extensão do Bit de Sinal
        elsif (opcode = "1100011") then  									-- Tipo SB
            S_imm(12)           <= instruction(31);          					-- Seleciona o imediato
            S_imm(11)           <= instruction(7);           					-- Seleciona o imediato
            S_imm(10 downto 5)  <= instruction(30 downto 25);  					-- Seleciona o imediato
            S_imm(4 downto 1)   <= instruction(11 downto 8);   					-- Seleciona o imediato
            S_imm(31 downto 13) <= (others => instruction(31));  				-- Extensão do Bit de Sinal
        end if;
    end process;

    immediate <= S_imm;  												-- Atribui o valor imeadiato à saída

end Behavioral;
*/

/* Code of Hazard:
library IEEE;
use IEEE.STD_LOGIC_1164.ALL;

entity Hazard is 
    port( 
        clk                 : IN std_logic;                          -- Entrada do sinal de clock
        MemRead_in          : IN std_logic;                          -- Sinal de controle que define quando a Memória será lida
        Rd_EX               : IN std_logic_vector(4 downto 0);       -- Rd é o endereço de destino da operação feita pelo CPU após o estágio de EX
        Rs1, Rs2            : IN std_logic_vector(4 downto 0);       -- Rs1 e Rs2 são os endereços dos registradores contidos na instrução
        stall               : OUT std_logic                          -- Saída que indica se um "stall" (atraso) deve ser aplicado no pipeline
    );
end Hazard;

architecture Behavioral of Hazard is

    signal stall_interno : std_logic := '0';  -- Signal temporário que armazena o nível lógico do stall

begin
    process(clk)
    begin
        if ((MemRead_in = '1') and ((Rd_EX = Rs1) or (Rd_EX = Rs2))) then        -- Fórmula do livro, página 322
            stall_interno <= '1';                                                -- Se o sinal de controle de MemRead_in for igual a 1 e o resultado  
        end if;                                                                  -- do estágio de Execution estiver em Rs1 ou Rs2, realiza um stall
    end process;

    stall <= stall_interno;                                                     -- Atribui o valor do signal temporário stall_interno à saída stall

end Behavioral;
*/

/* Code of IDEX:
LIBRARY ieee;
USE ieee.std_logic_1164.all;

ENTITY IDEX IS
  PORT (
    CLK             : IN std_logic;                             
    ALUSrc_in       : IN std_logic;                             
    ALUOp_in        : IN std_logic_vector(1 downto 0);          
    funct3_in       : IN std_logic_vector(2 downto 0);          
    funct7_in       : IN std_logic_vector(6 downto 0);          
    PC_in           : IN std_logic_vector(31 DOWNTO 0);         
    Soma_PC_in      : IN std_logic;                             
    Branch_in       : IN std_logic;                             
    MemWrite_in     : IN std_logic;                             
    MemRead_in      : IN std_logic;                             
    RegWrite_in     : IN std_logic;                             
    MemToReg_in     : IN std_logic;                             
    read1_in        : IN std_logic_vector(31 DOWNTO 0);         
    read2_in        : IN std_logic_vector(31 DOWNTO 0);         
    immediate_in    : in std_logic_vector(31 DOWNTO 0);         
    Rd_in           : IN std_logic_vector(4 DOWNTO 0);          
    Opcode_in       : IN std_logic_vector(6 DOWNTO 0);          
    JumpReg_in      : IN std_Logic;                             
    Rs1_In          : IN std_logic_vector(4 DOWNTO 0);          
    Rs2_In          : IN std_logic_vector(4 DOWNTO 0);          
    mode_in         : in std_logic;                             
    vecsize_in      : in std_logic_vector(1 downto 0);          

    ALUSrc_out      : out std_logic;                            
    ALUOp_out       : out std_logic_vector(1 downto 0);         
    funct3_out      : out std_logic_vector(2 downto 0);         
    funct7_out      : out std_logic_vector(6 downto 0);         
    PC_out          : out std_logic_vector(31 DOWNTO 0);        
    Soma_PC_out     : out std_logic;                            
    Branch_out      : out std_logic;                            
    MemWrite_out    : out std_logic;                            
    MemRead_out     : out std_logic;                            
    RegWrite_out    : out std_logic;                            
    MemToReg_out    : out std_logic;                            
    read1_out       : out std_logic_vector(31 DOWNTO 0);        
    read2_out       : out std_logic_vector(31 DOWNTO 0);        
    immediate_out   : out std_logic_vector(31 DOWNTO 0);        
    Rd_out          : out std_logic_vector(4 DOWNTO 0);         
    Opcode_out      : out std_logic_vector(6 DOWNTO 0);         
    JumpReg_out     : out std_Logic;                            
    Rs1_out         : out std_logic_vector(4 DOWNTO 0);         
    Rs2_out         : out std_logic_vector(4 DOWNTO 0);         
    mode_out        : out std_logic;                            
    vecsize_out     : out std_logic_vector(1 downto 0)          
  );  
END IDEX;

ARCHITECTURE TypeArchitecture OF IDEX IS

  SIGNAL idex_sig : std_logic_vector(173 DOWNTO 0);  -- 174 bits

BEGIN

  PROCESS (CLK)
  BEGIN
    IF (rising_edge(CLK)) THEN
      idex_sig(0) <= ALUSrc_in;          
      idex_sig(2 downto 1) <= ALUOp_in;          
      idex_sig(5 DOWNTO 3) <= funct3_in;      
      idex_sig(12 DOWNTO 6) <= funct7_in;
      idex_sig(44 DOWNTO 13) <= PC_in ;  
      idex_sig(45) <= Soma_PC_in;       
      idex_sig(46) <= Branch_in;   
      idex_sig(47) <= MemWrite_in;   
      idex_sig(48) <= MemRead_in;   
      idex_sig(49) <= RegWrite_in;   
      idex_sig(50) <= MemToReg_in;   
      idex_sig(82 DOWNTO 51) <= read1_in;    
      idex_sig(114 DOWNTO 83) <= read2_in;    
      idex_sig(146 DOWNTO 115) <= immediate_in;   
      idex_sig(151 DOWNTO 147) <= Rd_in;              -- Corrigido
      idex_sig(158 downto 152) <= Opcode_in;          -- Corrigido deslocamento
      idex_sig(159) <= JumpReg_in;  
      idex_sig(164 downto 160) <= Rs1_In;
      idex_sig(169 downto 165) <= Rs2_In;
      idex_sig(170) <= mode_in;        
      idex_sig(172 downto 171) <= vecsize_in;   
    END IF;

    IF (falling_edge(CLK)) THEN
      ALUSrc_out <= idex_sig(0);       
      ALUOp_out  <= idex_sig(2 downto 1);     
      funct3_out <= idex_sig(5 DOWNTO 3);      
      funct7_out <= idex_sig(12 DOWNTO 6);    
      PC_out <= idex_sig(44 DOWNTO 13);
      Soma_PC_out <= idex_sig(45);
      Branch_out <= idex_sig(46);
      MemWrite_out <= idex_sig(47);
      MemRead_out <= idex_sig(48);
      RegWrite_out <= idex_sig(49);
      MemToReg_out <= idex_sig(50);
      read1_out <= idex_sig(82 DOWNTO 51);
      read2_out <= idex_sig(114 DOWNTO 83);
      immediate_out <= idex_sig(146 DOWNTO 115);
      Rd_out <= idex_sig(151 DOWNTO 147);          -- Corrigido
      Opcode_out <= idex_sig(158 downto 152);      -- Corrigido deslocamento
      JumpReg_out <= idex_sig(159);
      Rs1_out <= idex_sig(164 downto 160);
      Rs2_out <= idex_sig(169 downto 165);
      mode_out <= idex_sig(170);
      vecsize_out <= idex_sig(172 downto 171);
    END IF;
  END PROCESS;

END TypeArchitecture;
*/

/* Code of ALU_Control:
library IEEE;
use IEEE.STD_LOGIC_1164.ALL;

entity ALU_Control is
    port(
        Funct7    		: IN std_logic_vector(6 downto 0);    	 -- Entrada do funct7
        Funct3    		: IN std_logic_vector(2 downto 0);    	 -- Entrada do funct3
        Opcode    		: IN std_logic_vector(6 downto 0);   	 -- Entrada do opcode
        AluOp   		: IN std_logic_vector(1 downto 0);       -- Entrada de códigos de operação da ALU (2 bits)
        ALU_Controle 	: OUT std_logic_vector(3 downto 0);      -- Saída do controle da ALU (4 bits)
        Beq_Bne		: OUT std_logic					 -- Sinal de controle para verificação de Beq ou Bne
        );
end ALU_Control;

architecture TypeArchitecture of ALU_Control is
begin

	ALU_Controle <= "0010" when AluOp = "00" else 	-- Operação de Load
			 	 "0110" when AluOp = "01" else 	-- Operação de Branch
			 	 "0010" when Funct7 = "0000000" and Funct3 = "000" else 	-- Operação de Soma
			 	 "0110" when Funct7 = "0100000" and Funct3 = "000" else 	-- Operação de Subtração
			 	 "0011" when Funct7 = "0000000" and Funct3 = "001" else 	-- Operação de Shift Left
			 	 "0101" when Funct7 = "0000000" and Funct3 = "100" else 	-- Operação XOR
			 	 "0111" when Funct7 = "0000000" and Funct3 = "101" else 	-- Operação de Shift Right
			 	 "0001" when Funct7 = "0000000" and Funct3 = "110" else 	-- Operação OR
			 	 "0000" when Funct7 = "0000000" and Funct3 = "111"; 		-- Operação AND
	Beq_Bne <= '1' when opcode="1100011" and Funct3="000" else '0';			-- '1' quando a instrução for Beq
	 
end TypeArchitecture;
*/

/* Code of Somador:
LIBRARY ieee;
USE ieee.std_logic_1164.all;
USE IEEE.std_logic_unsigned.ALL; 

ENTITY Somador IS
  PORT (
    A, B        : IN  std_logic_vector(31 DOWNTO 0); 	-- Entrada de vetores de 32 bits
    Z           : OUT std_logic_vector(31 DOWNTO 0) 	-- Saída do vetor resultado da soma
    );
END Somador;

ARCHITECTURE TypeArchitecture OF somador IS

BEGIN

Z <= A + B; 									-- Vetor resultado da soma

END TypeArchitecture;
*/

/* Code of Forward:
library IEEE;
use IEEE.STD_LOGIC_1164.ALL;

entity Forward is 
    port( 
         clk                        : IN std_logic;                         
         regWrite_WB, regWrite_MEM  : IN std_logic;                         
         Rs1, Rs2                   : IN std_logic_vector(4 downto 0);      
         Rd_WB, Rd_Mem              : IN std_logic_vector(4 downto 0);      
         forwardA, forwardB         : OUT std_logic_vector(1 downto 0)      
     );
end Forward;

architecture TypeArchitecture of Forward is
    signal forwardA_interno, forwardB_interno : std_logic_vector(1 downto 0) := "00";   
begin
    process(clk)
    begin
        if rising_edge(clk) then
            forwardA_interno <= "00";  -- Reset dos sinais internos
            forwardB_interno <= "00";

            if ((regWrite_MEM = '1') and (Rd_Mem /= "00000") and (Rd_Mem = Rs1)) then
                forwardA_interno <= "10";   
            end if;

            if ((regWrite_MEM = '1') and (Rd_Mem /= "00000") and (Rd_Mem = Rs2)) then
                forwardB_interno <= "10";  
            end if;

            if ((regWrite_WB = '1') and (Rd_WB /= "00000") and (Rd_WB = Rs1)) then
                forwardA_interno <= "01";   
            end if;

            if ((regWrite_WB = '1') and (Rd_WB /= "00000") and (Rd_WB = Rs2)) then
                forwardB_interno <= "01";   
            end if;
        end if;
    end process;

    forwardA <= forwardA_interno;  
    forwardB <= forwardB_interno;
end TypeArchitecture;
*/

/* Code of ALU:
library IEEE;
use IEEE.STD_LOGIC_1164.ALL;
use ieee.numeric_std.ALL;
use IEEE.std_logic_unsigned.ALL;

entity ALU is
    port(
    A, B       : in std_logic_vector(31 downto 0);   -- Operandos A e B de 32 bits da ALU
    controle   : in std_logic_vector(3 downto 0);    -- Entrada responsável por determinar a operação da ALU
    resultado  : out std_logic_vector(31 downto 0);  -- Resultado da operação feita pela ALU
    f_zero     : out std_logic;                      -- Flag indicadora de resultado igual a zero na operacão da ALU
    mode       : in std_logic;                       -- Modo de operação: 0 para operação única e 1 para operação vetorial
    vecSize     : in std_logic_vector(1 downto 0)     -- Tamanho do vetor de operações (usado no modo vetorial)
    );
end ALU;


architecture TypeArchitecture of ALU is

-- Declaração dos sinais temporários da ALU
signal resultado_nv : std_logic_vector(31 downto 0); -- Resultado não vetorial
signal resultado_v  : std_logic_vector(31 downto 0); -- Resultado vetorial
signal soma_v       : std_logic_vector(31 downto 0); -- Sinal temporário que armazena o resultado final da soma vetorial
signal sub_v        : std_logic_vector(31 downto 0); -- Sinal temporário que armazena o resultado final da subtração vetorial
signal shiftL_v     : std_logic_vector(31 downto 0); -- Sinal temporário que armazena o resultado final do Shift Left vetorial
signal shiftR_v     : std_logic_vector(31 downto 0); -- Sinal temporário que armazena o resultado final da Shift Right vetorial

signal A16_1 : std_logic_vector(15 downto 0);  -- Vetor que contém os bits de índice 31 até 16 do operando quando vecsize='10' (16 bits)
signal A16_2 : std_logic_vector(15 downto 0);  -- Vetor que contém os bits de índice 15 até 0 do operando quando vecsize='10' (16 bits)

signal A8_1 : std_logic_vector(7 downto 0);  -- Vetor que contém os bits de índice 31 até 24 do operando quando vecsize='01' (8 bits)
signal A8_2 : std_logic_vector(7 downto 0);  -- Vetor que contém os bits de índice 23 até 16 do operando quando vecsize='01' (8 bits)
signal A8_3 : std_logic_vector(7 downto 0);  -- Vetor que contém os bits de índice 15 até 8 do operando quando vecsize='01' (8 bits)
signal A8_4 : std_logic_vector(7 downto 0);  -- Vetor que contém os bits de índice 7 até 0 do operando quando vecsize='01' (8 bits)

signal A4_1 : std_logic_vector(3 downto 0);  -- Vetor que contém os bits de índice 31 até 28 do operando quando vecsize='00' (4 bits)
signal A4_2 : std_logic_vector(3 downto 0);  -- Vetor que contém os bits de índice 27 até 24 do operando quando vecsize='00' (4 bits)
signal A4_3 : std_logic_vector(3 downto 0);  -- Vetor que contém os bits de índice 23 até 20 do operando quando vecsize='00' (4 bits)
signal A4_4 : std_logic_vector(3 downto 0);  -- Vetor que contém os bits de índice 19 até 16 do operando quando vecsize='00' (4 bits)
signal A4_5 : std_logic_vector(3 downto 0);  -- Vetor que contém os bits de índice 15 até 12 do operando quando vecsize='00' (4 bits)
signal A4_6 : std_logic_vector(3 downto 0);  -- Vetor que contém os bits de índice 11 até 8 do operando quando vecsize='00' (4 bits)
signal A4_7 : std_logic_vector(3 downto 0);  -- Vetor que contém os bits de índice 7 até 4 do operando quando vecsize='00' (4 bits)
signal A4_8 : std_logic_vector(3 downto 0);  -- Vetor que contém os bits de índice 3 até 0 do operando quando vecsize='00' (4 bits)

signal integer_B : integer;                  -- Integer do valor binário que entra como operando B

begin

    -- Conversão da entrada B para integer para uso nas operações de deslocamento
    integer_B <= to_integer(unsigned(B));

    -- Divisão do sinal de entrada A em subvetores para as operações vetoriais
    A16_1 <= A(31 downto 16);
    A16_2 <= A(15 downto 0);

    A8_1 <= A(31 downto 24);
    A8_2 <= A(23 downto 16);
    A8_3 <= A(15 downto 8);
    A8_4 <= A(7 downto 0);

    A4_1 <= A(31 downto 28);
    A4_2 <= A(27 downto 24);
    A4_3 <= A(23 downto 20);
    A4_4 <= A(19 downto 16);
    A4_5 <= A(15 downto 12);
    A4_6 <= A(11 downto 8);
    A4_7 <= A(7 downto 4);
    A4_8 <= A(3 downto 0);
    
    
    -- Cálculos das operações vetoriais com base no tamanho do vetor (vecsize)
    soma_v <= (A + B) when vecSize = "11" else
             ((A16_1 + B(31 downto 16)) & (A16_2 + B(15 downto 0))) when vecSize = "10" else
             ((A8_1 + B(31 downto 24)) & (A8_2 + B(23 downto 16)) & (A8_3 + B(15 downto 8)) & (A8_4 + B(7 downto 0))) when vecSize = "01" else
             ((A4_1 + B(31 downto 28)) & (A4_2 + B(27 downto 24)) & (A4_3 + B(23 downto 20)) & (A4_4 + B(19 downto 16)) & (A4_5 + B(15 downto 12)) & (A4_6 + B(11 downto 8)) & (A4_7 + B(7 downto 4)) & (A4_8 + B(3 downto 0))) when vecSize = "00";
    
    sub_v <= (A - B) when vecSize = "11" else
             ((A16_1 - B(31 downto 16)) & (A16_2 - B(15 downto 0))) when vecSize = "10" else
             ((A8_1 - B(31 downto 24)) & (A8_2 - B(23 downto 16)) & (A8_3 - B(15 downto 8)) & (A8_4 - B(7 downto 0))) when vecSize = "01" else
             ((A4_1 - B(31 downto 28)) & (A4_2 - B(27 downto 24)) & (A4_3 - B(23 downto 20)) & (A4_4 - B(19 downto 16)) & (A4_5 - B(15 downto 12)) & (A4_6 - B(11 downto 8)) & (A4_7 - B(7 downto 4)) & (A4_8 - B(3 downto 0))) when vecSize = "00";
    
    -- Cálculos das operações de deslocamento vetoriais
    shiftL_v <= (std_logic_vector(shift_left(unsigned(A), integer_B))) when vecSize = "11" else
             ((std_logic_vector(shift_left(unsigned(A16_1), integer_B))) & std_logic_vector(shift_left(unsigned(A16_2), integer_B))) when vecSize = "10" else
             ((std_logic_vector(shift_left(unsigned(A8_1), integer_B))) & (std_logic_vector(shift_left(unsigned(A8_2), integer_B))) & (std_logic_vector(shift_left(unsigned(A8_3), integer_B))) & (std_logic_vector(shift_left(unsigned(A8_4), integer_B)))) when vecSize = "01" else
             ((std_logic_vector(shift_left(unsigned(A4_1), integer_B))) & (std_logic_vector(shift_left(unsigned(A4_2), integer_B))) & (std_logic_vector(shift_left(unsigned(A4_3), integer_B))) & (std_logic_vector(shift_left(unsigned(A4_4), integer_B))) & (std_logic_vector(shift_left(unsigned(A4_5), integer_B))) & (std_logic_vector(shift_left(unsigned(A4_6), integer_B))) & (std_logic_vector(shift_left(unsigned(A4_7), integer_B))) & (std_logic_vector(shift_left(unsigned(A4_8), integer_B)))) when vecSize = "00";

    shiftR_v <= (std_logic_vector(shift_right(unsigned(A), integer_B))) when vecSize = "11" else
             ((std_logic_vector(shift_right(unsigned(A16_1), integer_B))) & std_logic_vector(shift_right(unsigned(A16_2), integer_B))) when vecSize = "10" else
             ((std_logic_vector(shift_right(unsigned(A8_1), integer_B))) & (std_logic_vector(shift_right(unsigned(A8_2), integer_B))) & (std_logic_vector(shift_right(unsigned(A8_3), integer_B))) & (std_logic_vector(shift_right(unsigned(A8_4), integer_B)))) when vecSize = "01" else
             ((std_logic_vector(shift_right(unsigned(A4_1), integer_B))) & (std_logic_vector(shift_right(unsigned(A4_2), integer_B))) & (std_logic_vector(shift_right(unsigned(A4_3), integer_B))) & (std_logic_vector(shift_right(unsigned(A4_4), integer_B))) & (std_logic_vector(shift_right(unsigned(A4_5), integer_B))) & (std_logic_vector(shift_right(unsigned(A4_6), integer_B))) & (std_logic_vector(shift_right(unsigned(A4_7), integer_B))) & (std_logic_vector(shift_right(unsigned(A4_8), integer_B)))) when vecSize = "00";
    

    -- ALU vetorial (mode = 1) 
    resultado_v <= soma_v when controle = "0010" else
                sub_v when controle = "0110" else
                shiftL_v when controle = "0011" else
                shiftR_v when controle = "0111" else
                (others => '0');
    
    -- ALU não vetorial (mode = 0)
    resultado_nv <= (A + B) when controle = "0010" else
                   (A - B) when controle = "0110" else
                   (A XOR B) when controle = "0101" else
                   (A OR B) when controle = "0001" else
                   (A AND B) when controle = "0000" else
                   (std_logic_vector(shift_left(unsigned(A), integer_B))) when controle = "0011" else
                   (std_logic_vector(shift_right(unsigned(A), integer_B))) when controle = "0111";
    
    -- Seleção do resultado de acordo com o sinal de controle "mode"
    resultado <= resultado_nv when mode = '0' else
                resultado_v when mode = '1';
                
    -- Sinalização se o resultado é zero (serve para o Branch) -> como as operações vetoriais não incluem Branch, basta verificar do resultado não vetorial
    f_zero <= '1' when resultado_nv = "00000000000000000000000000000000" else '0';   

end TypeArchitecture;
*/

/* Code of EXMEM:
LIBRARY ieee;
USE ieee.std_logic_1164.all;

ENTITY EXMEM IS
  PORT (
    CLK             : IN std_logic;                             -- Entrada do sinal de clock            
    Branch_in       : IN std_logic;                             -- Entrada do sinal de controle que define quando ocorre Branch
    MemWrite_in     : IN std_logic;                             -- Entrada do sinal de controle que define quando a Memória será escrita
    MemRead_in      : IN std_logic;                             -- Entrada do sinal de controle que define quando a Memória será lida
    RegWrite_in     : IN std_logic;                             -- Entrada do sinal de controle que define quando o registrador será escrito
    MemToReg_in     : IN std_logic;                             -- Entrada do sinal de controle que define quando um dado será passado da memória para o registrador
    New_PC_in       : IN std_logic_vector(31 DOWNTO 0);         -- Soma do PC com imediato (jal) ou reg com imediato substituindo PC (jalr)
    Zero_in         : IN std_logic;                             -- Quando o resultado da ALU foi zero (serve para Branch)
    ALUresult_in    : IN std_logic_vector(31 DOWNTO 0);         -- Entrada do resultado da operação da ALU
    read2_in        : IN std_logic_vector(31 DOWNTO 0);         -- Entrada do valor lido do read data 2
    Rd_in           : IN std_logic_vector(4 DOWNTO 0);          -- Entrada da instrução atual buscada na memória de instruções
    Jalr_ou_Jal_in	: IN std_logic;					    -- Entrada que indica se é Jalr ou Jal	
  
    Branch_out      : out std_logic;                            -- Saída do sinal de controle que define quando ocorre Branch 
    MemWrite_out    : out std_logic;                            -- Saída do sinal de controle que define quando a Memória será escrita
    MemRead_out     : out std_logic;                            -- Saída do sinal de controle que define quando a Memória será lida
    RegWrite_out    : out std_logic;                            -- Saída do sinal de controle que define quando o registrador será escrito
    MemToReg_out    : out std_logic;                            -- Saída do sinal de controle que define quando um dado será passado da memória para o registrador
    New_PC_out       : out std_logic_vector(31 DOWNTO 0);        -- Soma do PC com imediato (jal) ou reg com imediato substituindo PC (jalr)
    Zero_out        : out std_logic;                            -- Quando o resultado da ALU foi zero (serve para Branch)
    ALUresult_out   : out std_logic_vector(31 DOWNTO 0);        -- Saída do resultado da operação da ALU
    read2_out       : out std_logic_vector(31 DOWNTO 0);        -- Saída do valor lido do read data 2
    Rd_out          : out std_logic_vector(4 DOWNTO 0);          -- Saída da instrução atual buscada na memória de instruções
    Jalr_ou_Jal_out	: out std_logic					    -- Saída que indica se é Jalr ou Jal
    );
END EXMEM;


ARCHITECTURE TypeArchitecture OF EXMEM IS

SIGNAL exmem_sig : std_logic_vector(107 DOWNTO 0);  -- Registrador de 192 bits para armazenar os valores do EXMEM

BEGIN

    PROCESS (CLK)
    BEGIN
        IF (rising_edge(CLK)) THEN                   -- Detecta a borda de subida do sinal de clock
            exmem_sig(0)    <= Branch_in;          
            exmem_sig(1)    <= MemWrite_in;          
            exmem_sig(2)   <= MemRead_in;      
            exmem_sig(3)   <= RegWrite_in;
            exmem_sig(4)   <= MemToReg_in;  
            exmem_sig(36 downto 5)    <= New_PC_in;       
            exmem_sig(37)           <= Zero_in;   
            exmem_sig(69 downto 38)    <= ALUresult_in;   
            exmem_sig(101 downto 70)    <= read2_in;   
            exmem_sig(106 downto 102)    <= Rd_in;   
            exmem_sig(107) <= Jalr_ou_Jal_in;
        END IF;
        IF (falling_edge(CLK)) THEN                 -- Detecta a borda de descida do sinal de clock
            Branch_out    <= exmem_sig(0);       
            MemWrite_out  <= exmem_sig(1);     
            MemRead_out  <= exmem_sig(2);      
            RegWrite_out <= exmem_sig(3);    
            MemToReg_out <= exmem_sig(4);
            New_PC_out <= exmem_sig(36 downto 5);
            Zero_out <= exmem_sig(37);
            ALUresult_out <= exmem_sig(69 downto 38);
            read2_out <= exmem_sig(101 downto 70);
            Rd_out <= exmem_sig(106 downto 102);
            Jalr_ou_Jal_out <= exmem_sig(107);
        END IF;
    END PROCESS;

    
END TypeArchitecture;
*/

/* Code of MEMWB:
LIBRARY ieee;
USE ieee.std_logic_1164.all;

ENTITY MEMWB IS
  PORT (
    CLK             : IN std_logic;                             -- Entrada do sinal de clock            
    RegWrite_in     : IN std_logic;                             -- Entrada do sinal de controle que define quando o registrador será escrito
    MemToReg_in     : IN std_logic;                             -- Entrada do sinal de controle que define quando um dado será passado da memória para o registrador
    Mem_data_in     : IN std_logic_vector(31 DOWNTO 0);         -- Entrada do valor lido na memória
    ALUresult_in    : IN std_logic_vector(31 DOWNTO 0);         -- Entrada do resultado da operação da ALU
    Rd_in           : IN std_logic_vector(4 DOWNTO 0);          -- Entrada da instrução atual buscada na memória de instruções
  
    RegWrite_out    : out std_logic;                            -- Saída do sinal de controle que define quando o registrador será escrito
    MemToReg_out    : out std_logic;                            -- Saída do sinal de controle que define quando um dado será passado da memória para o registrador
    Mem_data_out    : out std_logic_vector(31 DOWNTO 0);        -- Saída do valor lido na memória
    ALUresult_out   : out std_logic_vector(31 DOWNTO 0);        -- Saída do resultado da operação da ALU
    Rd_out          : out std_logic_vector(4 DOWNTO 0)          -- Saída da instrução atual buscada na memória de instruções
    );
END MEMWB;


ARCHITECTURE TypeArchitecture OF MEMWB IS

SIGNAL memwb_sig : std_logic_vector(70 DOWNTO 0);  -- Registrador de 70 bits para armazenar os valores do memwb

BEGIN

    PROCESS (CLK)
    BEGIN
        IF (rising_edge(CLK)) THEN                   -- Detecta a borda de subida do sinal de clock     
            memwb_sig(0)   <= RegWrite_in;
            memwb_sig(1)   <= MemToReg_in;  
            memwb_sig(33 downto 2)  <= Mem_data_in ;       
            memwb_sig(65 downto 34)  <= ALUresult_in;   
            memwb_sig(70 downto 66)  <= Rd_in;   
        END IF;
        IF (falling_edge(CLK)) THEN                 -- Detecta a borda de descida do sinal de clock
            RegWrite_out <= memwb_sig(0);    
            MemToReg_out <= memwb_sig(1);
            Mem_data_out <= memwb_sig(33 downto 2);
            ALUresult_out <= memwb_sig(65 downto 34);
            Rd_out <= memwb_sig(70 downto 66);
        END IF;
    END PROCESS;

    
END TypeArchitecture;
*/
