// Digital circuit somador_avx.dig as structural Verilog
module somador_avx (
  input  [31:0] A_i,
  input  [31:0] B_i,
  input  mode_i,
  input  [1:0] vecSize_i,
  output [31:0] S_o
);

  somador_avx #(.applicationType("GHDL")) u_somador_avx (
    .A_i(A_i), .B_i(B_i), .mode_i(mode_i), .vecSize_i(vecSize_i), .S_o(S_o));
endmodule

/* Code of somador_avx:
library ieee;
use ieee.std_logic_1164.all;

entity somador_avx is
	port (
		A_i	: IN std_logic_vector(31 downto 0); -- Entrada A_i
		B_i	: IN  std_logic_vector(31 downto 0); -- Entrada B_i
		mode_i	: IN std_logic; -- Operacao (soma ou subtracao)
		vecSize_i : IN std_logic_vector(1 downto 0); -- tamanho do vetor (4, 8, 16 ou 32 bits)

		S_o : OUT std_logic_vector(31 downto 0) -- saida (resultado da operacao)
	);
end somador_avx;

architecture calculator of somador_avx is
	signal criate  : std_logic_vector(31 downto 0); -- 1+1 (cria carry)
	signal passing : std_logic_vector(31 downto 0); -- carry lookahead
	signal carry   : std_logic_vector(31 downto 0); -- carry
	signal B_adj   : std_logic_vector(31 downto 0); -- entrada B ajustada
begin

	process(all)
		variable x : std_logic;
	begin
		-- barra a segunda entrada(B_i) se a operacao for uma subtracao (complemento de 2) 
		if mode_i = '1' then
			B_adj <= not B_i; -- barra B_i
			carry(0) <= '1'; -- soma 1
			x := '1';
		else
			B_adj <= B_i;
			carry(0) <= '0';
			x := '0';
		end if;

		---------------------------------------------------------------
		-- ajustando o carry e os auxiliares
		for item in 0 to 31 loop
			criate(item)  <= (A_i(item) and B_adj(item));
			passing(item) <= (A_i(item) or B_adj(item));
		end loop;
		
		-- mudar bits de 1 a 3
		for i in 1 to 3 loop
			carry(i) <= (criate(i-1) or (passing(i-1) and carry(i-1))); 
		end loop;
		
		-- mudar bit 4
		if vecSize_i = "00" then
			carry(4) <= x;
		else
			carry(4) <= (criate(3) or (passing(3) and carry(3)));
		end if;
		
		-- mudar bits de 5 a 7
		for i in 5 to 7 loop
			carry(i) <= (criate(i-1) or (passing(i-1) and carry(i-1))); 
		end loop;
		
		-- mudar bit 8
		if vecSize_i = "00" or vecSize_i = "01" then
			carry(8) <= x;
		else
			carry(8) <= (criate(7) or (passing(7) and carry(7)));
		end if;
		
		-- mudar bits de 9 a 11
		for i in 9 to 11 loop
			carry(i) <= (criate(i-1) or (passing(i-1) and carry(i-1))); 
		end loop;
		
		-- mudar bit 12
		if vecSize_i = "00" then
			carry(12) <= x;
		else
			carry(12) <= (criate(11) or (passing(11) and carry(11)));
		end if;
		
		-- mudar bits de 13 a 15
		for i in 13 to 15 loop
			carry(i) <= (criate(i-1) or (passing(i-1) and carry(i-1))); 
		end loop;
		
		-- mudar bit 16
		if vecSize_i = "00" or vecSize_i = "01" or vecSize_i = "10" then
			carry(16) <= x;
		else
			carry(16) <= (criate(15) or (passing(15) and carry(15)));
		end if;
		
		-- mudar bits de 17 a 19
		for i in 17 to 19 loop
			carry(i) <= (criate(i-1) or (passing(i-1) and carry(i-1))); 
		end loop;
		
		-- mudar bit 20
		if vecSize_i = "00" then
			carry(20) <= x;
		else
			carry(20) <= (criate(19) or (passing(19) and carry(19)));
		end if;
		
		-- mudar bits de 21 a 23
		for i in 21 to 23 loop
			carry(i) <= (criate(i-1) or (passing(i-1) and carry(i-1))); 
		end loop;
		
		-- mudar bit 24
		if vecSize_i = "00" or vecSize_i = "01" then
			carry(24) <= x;
		else
			carry(24) <= (criate(23) or (passing(23) and carry(23)));
		end if;
		
		-- mudar bits de 25 a 27
		for i in 25 to 27 loop
			carry(i) <= (criate(i-1) or (passing(i-1) and carry(i-1))); 
		end loop;
 		
		-- mudar bit 28
		if vecSize_i = "00" then
			carry(28) <= x;
		else
			carry(28) <= (criate(27) or (passing(27) and carry(27)));
		end if;
		
		-- mudar bits de 29 a 31
		for i in 29 to 31 loop
			carry(i) <= (criate(i-1) or (passing(i-1) and carry(i-1)));
		end loop;
		---------------------------------------------------------------
	end process;

	-- resultado (S_o)
	soma: for j in 0 to 31 generate
		S_o(j) <= (A_i(j) xor B_adj(j) xor carry(j));
	end generate soma;

end calculator;
*/
